// Logisim project 8bitCPU_t2.circ as structural Verilog: 2 circuits, main circuit main
module main (
);

  wire and_1_out;

  // AND_Gate and_1 has open pins: out=and_1_out
  // AND_Gate and_2 is placed but not wired
  // NAND_Gate nand_1 is placed but not wired
  // ALU alu_1: pin names not known; wires that end beside it: and_1_out
endmodule

module ALU (
  input  [7:0] A,
  input  [7:0] B,
  input  [2:0] in_3,
  input  [2:0] in_4,
  input  in_5,
  output [7:0] outALU,
  output cout,
  output out_8
);

  wire [7:0] adder_1_out, and_1_out, not_1_out, or_1_out, shifter_1_out, shifter_2_out, subtractor_1_out,
       xor_1_out;

  Adder adder_1 (.a(A), .b(B), .out(adder_1_out), .cout(cout));  // open: cin
  Subtractor subtractor_1 (.a(A), .b(B), .out(subtractor_1_out), .bout(out_8));  // open: bin
  Shifter shifter_1 (.in(A), .\dist (in_3), .out(shifter_1_out));
  Shifter #(.shift("lr")) shifter_2 (.in(A), .\dist (in_3), .out(shifter_2_out));
  assign not_1_out = ~A;  // NOT_Gate not_1, 8 bits wide
  assign and_1_out = A & B;  // AND_Gate and_1, 8 bits wide
  assign or_1_out = B | B;  // OR_Gate or_1, 8 bits wide
  assign xor_1_out = A ^ B;  // XOR_Gate xor_1, 8 bits wide
  Multiplexer #(.enable("true"), .select(3), .width(8)) multiplexer_1 (
    .in0(adder_1_out), .in1(subtractor_1_out), .in2(shifter_1_out), .in3(shifter_2_out), .in4(and_1_out),
    .in5(or_1_out), .in6(not_1_out), .in7(xor_1_out), .out(outALU), .sel(in_4), .en(in_5));
endmodule
